# Fritzing sketch MCP23017TestBed (saved by Fritzing 0.9.4)
breadboards: 1

parts:
  IC1 = MCP23017 I2C I/O Expander
  R1 = Resistor [tolerance=±5% resistance=4.7k package=THT]
  R2 = Resistor [tolerance=±5% resistance=4.7k package=THT]
  LED1 = LED - 5mm [color="Blue (470nm)" package="5 mm [THT]"]
  R3 = Resistor [tolerance=±5% resistance=220 package=THT]
  R4 = Resistor [tolerance=±5% resistance=220 package=THT]
  RE1 = Rotary Encoder [package=THT]
  RE2 = Rotary Encoder [package=THT]
  RE3 = Rotary Encoder [package=THT]
  RE4 = Rotary Encoder [package=THT]
  RE5 = Rotary Encoder [package=THT]
  Part1 = Arduino Mega 2560 (Rev3)

nets:
  N1: IC1.GPB0, RE5.EncoderPinA
  N2: IC1.GPB1, RE5.EncoderPinB
  VDD: IC1.VDD, R1.Pin_1, R2.Pin_1, LED1.anode, R4.Pin_0, RE1.EncoderPinC, RE2.EncoderPinC, RE3.EncoderPinC, RE4.EncoderPinC, RE5.EncoderPinC, Part1.5V
  VSS: IC1.VSS, IC1.A0, IC1.A1, IC1.A2, Part1.GND
  N3: IC1.SCL, R1.Pin_0, Part1.D21/SCL
  N4: IC1.SDA, R2.Pin_0, Part1.D20/SDA
  N5: IC1.RESET, R4.Pin_1
  N6: IC1.INTB, R3.Pin_0
  N7: IC1.GPA0, RE1.EncoderPinB
  N8: IC1.GPA1, RE1.EncoderPinA
  N9: IC1.GPA2, RE2.EncoderPinB
  N10: IC1.GPA3, RE2.EncoderPinA
  N11: IC1.GPA4, RE3.EncoderPinB
  N12: IC1.GPA5, RE3.EncoderPinA
  N13: IC1.GPA6, RE4.EncoderPinB
  N14: IC1.GPA7, RE4.EncoderPinA
  N15: LED1.cathode, R3.Pin_1

notes:
  Untested!  Use Caution!

custom parts:
  MCP23017 I2C I/O Expander: The MCP23017 uses two i2c pins (these can be shared with other i2c devices), and in exchange gives you 16 general purpose pins. You can set each of 16 pins to be input, output, input with a pullup or open drain. There's even the ability to get an interrupt via an external pin when any of the inputs change so you don't have to keep polling the chip.
